# Fritzing sketch The_Internet (saved by Fritzing 0.9.3b)
breadboards: 1

parts:
  Part1 = Lithium Ion Polymer Battery 3.7v 2500mAh [part_number=328]
  Part2 = Adafruit USB LiIon/LiPoly Charger [part_number="Adafruit #259"]
  U1 = attiny85 [package=dip]
  C1 = Electrolytic Capacitor [capacitance=47µF package="0405 [SMD, electrolytic]"]
  C2 = Ceramic Capacitor [capacitance=0.1µF package="1206 [SMD, multilayer]"]
  IC1 = Voltage Regulator [package=to-92]
  LED1 = RGB LED (com. cathode, rbg) [package="5 mm [THT]"]
  R1 = Resistor [tolerance=±5% resistance=330 package="2010 [SMD]"]
  U2 = mystery part, 4 pins [chip_label="Power Boost"]
  R2 = Resistor [tolerance=±5% resistance=10k package="2010 [SMD]"]
  LED2 = LED - 3mm [color="Red (633nm)" package="3 mm [THT]"]
  R3 = Resistor [tolerance=±5% resistance=10k package="2010 [SMD]"]

nets:
  N1: Part1.positive, Part2.BATT, U2.pin1
  GND: Part1.negative, Part2.GND, U1.Pin_4, C1.-, C2.0, IC1.GND, LED1.common_cathode, U2.pin2, U2.pin4
  N2: Part2.5.0V, R1.Pin_0
  N3: Part2.STAT1, LED1.blue_anode
  N4: Part2.STAT2, LED1.green_anode
  N5: U1.Pin_1, R2.Pin_0
  N6: U1.Pin_5, R3.Pin_0
  5V: U1.Pin_8, IC1.OUT, R2.Pin_1, LED2.anode
  9V: C1.+, C2.1, IC1.IN, U2.pin3
  N7: LED1.red_anode, R1.Pin_1
  N8: LED2.cathode, R3.Pin_1

notes:
  Power Supply
  Battery Charger /Status LEDs
  Microcontroller and LED

custom parts:
  Lithium Ion Polymer Battery 3.7v 2500mAh: Lithium ion polymer (also known as 'lipo' or 'lipoly') batteries are thin, light and powerful. The output ranges from 4.2V when completely charged to 3.7V. This battery has a capacity of 2500mAh for a total of about 10 Wh. The batteries come pre-attached with a genuine 2-pin JST-PH connector as shown and include the necessary protection circuitry.
  Adafruit USB LiIon/LiPoly Charger: This is a Lithium Ion and Lithium Polymer battery charger based on the MCP73833. It uses a USB mini-B for connection to any computer or 'USB wall adapter'. Charging is performed in three stages: first a preconditioning charge, then a constant-current fast charge and finally a constant-voltage trickle charge to keep the battery topped-up. The fast-charge current is 500mA by default, but is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
